# Fritzing sketch Controller (saved by Fritzing 0.9.3b)
breadboards: 1

parts:
  Onderdeel1 = Arduino Uno (Rev3)
  S1 = Tilt Switch [package=THT]
  R1 = Resistor [tolerance=±5% resistance=220 package="2512 [SMD]"]
  R2 = Rotary Potentiometer (Small) [maximum_resistance=100kΩ package=THT]
  LED1 = LED - 3mm [color="Yellow (595nm)" package="3 mm [THT]"]
  LED2 = LED - 3mm [color="Blue (525nm)" package="3 mm [THT]"]
  LED3 = LED - 3mm [color="Green (555nm)" package="3 mm [THT]"]
  LED4 = LED - 3mm [color="Red (633nm)" package="3 mm [THT]"]
  S2 = Pushbutton [package="[SMD]"]
  R3 = Resistor [tolerance=±5% resistance=220 package="2512 [SMD]"]

nets:
  N1: Onderdeel1.A0, R2.wiper
  N2: Onderdeel1.D10_PWM/SS, LED3.anode
  N3: Onderdeel1.D11_PWM/MOSI, LED2.anode
  N4: Onderdeel1.D12/MISO, LED4.anode
  N5: Onderdeel1.D13/SCK, LED1.anode
  N6: Onderdeel1.D2, S2.Pin_3, S2.Pin_4, R3.Pin_1
  N7: Onderdeel1.D3_PWM, S1.Pin_2, R1.Pin_1
  N8: Onderdeel1.5V, R2.leg1, S2.Pin_1, S2.Pin_2, R3.Pin_0
  N9: Onderdeel1.GND, S1.Pin_1, R1.Pin_0, R2.leg2, LED1.cathode, LED2.cathode, LED3.cathode, LED4.cathode
