# Fritzing sketch examen (saved by Fritzing 0.9.3b)
breadboards: 1

parts:
  Onderdeel1 = Arduino Uno (Rev3) - ICSP
  S1 = Pushbutton [package="[THT]"]
  R1 = Resistor [tolerance=±5% resistance=220 package=THT]
  LED1 = LED - 5mm [color="Orange (605nm)" package="5 mm [THT]"]  # not connected
  LED2 = LED - 5mm [color="Red (633nm)" package="5 mm [THT]"]  # not connected
  LED4 = LED - 5mm [color="Green (570nm)" package="5 mm [THT]"]  # not connected
  LED3 = LED - 5mm [color="Blue (525nm)" package="5 mm [THT]"]
  S2 = Tilt Switch [package=THT]  # not connected
  R2 = Resistor [tolerance=±5% resistance=220 package=THT]
  R3 = Rotary Potentiometer (Small) [maximum_resistance=100kΩ package=THT]  # not connected

nets:
  N1: Onderdeel1.5V, Onderdeel1.D10_PWM/SS, Onderdeel1.D11_PWM/MOSI, Onderdeel1.D12/MISO, Onderdeel1.D13/SCK, R1.Pin_1, R2.Pin_1
  N2: Onderdeel1.GND, S1.Pin_3, S1.Pin_4, LED3.anode
