# Fritzing sketch Displayer (saved by Fritzing 0.9.3b)
breadboards: 1

parts:
  Onderdeel1 = Arduino Uno (Rev3) - ICSP
  Onderdeel2 = Bluetooth HC-05 Macho
  R1 = Resistor [tolerance=±5% resistance=220 package="1206 [SMD]"]
  R2 = Resistor [tolerance=±5% resistance=220 package="1206 [SMD]"]
  R3 = Resistor [tolerance=±5% resistance=220 package="1206 [SMD]"]
  U1 = LCD-16X2 [package=lcd-16x2_noholes]
  R4 = Resistor [tolerance=±5% resistance=220 package="1206 [SMD]"]
  R5 = Rotary Potentiometer (Small) [maximum_resistance=100kΩ package=THT]
  J1 = Piezo Speaker
  LED1 = LED - 3mm [color="Red (633nm)" package="3 mm [THT]"]
  LED2 = LED - 3mm [color="Green (560nm)" package="3 mm [THT]"]

nets:
  N1: Onderdeel1.D8, U1.DB4
  N2: Onderdeel1.D9_PWM, U1.RS
  N3: Onderdeel1.D10_PWM/SS, U1.E
  N4: Onderdeel1.D11_PWM/MOSI, LED1.anode
  N5: Onderdeel1.D12/MISO, J1.pin2
  N6: Onderdeel1.D13/SCK, LED2.anode
  N7: Onderdeel1.D3_PWM, Onderdeel2.TXD
  N8: Onderdeel1.D4, R1.Pin_0
  N9: Onderdeel1.D5_PWM, U1.DB7
  N10: Onderdeel1.D6_PWM, U1.DB6
  N11: Onderdeel1.D7, U1.DB5
  5V: Onderdeel1.5V, Onderdeel2.VCC, R2.Pin_0, R3.Pin_1, U1.VDD, R4.Pin_0, R5.leg1, J1.pin1
  GND: Onderdeel1.GND, Onderdeel2.GND, U1.VSS, U1.R_W, U1.K, R5.leg2, LED1.cathode, LED2.cathode
  N12: Onderdeel2.RXD, R1.Pin_1
  N13: R2.Pin_1, R3.Pin_0
  N14: U1.VO, R5.wiper
  N15: U1.A, R4.Pin_1
